# Fritzing sketch Ike Nurhayati (saved by Fritzing 0.9.3b)
breadboards: 1

parts:
  Part1 = Arduino Uno (Rev3)
  LED1 = LED - 5mm [color="Blue (470nm)" package="5 mm [THT]"]
  LED2 = LED - 5mm [color="Blue (470nm)" package="5 mm [THT]"]
  LED3 = LED - 5mm [color="Blue (470nm)" package="5 mm [THT]"]
  R1 = Resistor [tolerance=±5% resistance=220 package=THT]
  R2 = Photocell (LDR) [package=THT]

nets:
  N1: Part1.A0, R1.Pin_1, R2.pin_0
  N2: Part1.D12/MISO, LED3.anode
  N3: Part1.D2, LED1.anode
  N4: Part1.D6_PWM, LED2.anode
  N5: Part1.GND, LED1.cathode, LED2.cathode, LED3.cathode, R1.Pin_0, R2.pin_1
